# Fritzing sketch LED (saved by Fritzing 0.8.3b)
breadboards: 1

parts:
  R1 = Resistor [tolerance=±5% resistance=180 package=THT]
  R3 = Resistor [tolerance=±5% resistance=100 package=THT]
  R2 = Resistor [tolerance=±5% resistance=100 package=THT]
  LED1 = RGB LED (com. cathode, rgb) [package="5 mm [THT]"]

nets:
  N1: R1.Pin_0, R1.Pin_1, LED1.red_anode
  N2: R3.Pin_0, R3.Pin_1, LED1.green_anode
  N3: R2.Pin_0, R2.Pin_1, LED1.blue_anode
  GND: LED1.common_cathode
