# Fritzing sketch MODI (saved by Fritzing 0.8.3b)
breadboards: 1

parts:
  Microcontrolador_Arduino = Arduino Fio (Funnel I/O)
  Driver_motores = TB6612FNG Breakout v11
  MB = DC Motor
  MA = DC Motor
  LED_RGB = RGB LED (com. cathode, rbg) [package="5 mm [THT]"]
  R1 = Resistor [tolerance=±5% resistance=180 package=THT]
  R2 = Resistor [tolerance=±5% resistance=100 package=THT]
  R3 = Resistor [tolerance=±5% resistance=100 package=THT]

nets:
  VCC: Microcontrolador_Arduino.VCC, Driver_motores.VCC
  GND: Microcontrolador_Arduino.GND, Driver_motores.GND, LED_RGB.common_cathode
  N1: Microcontrolador_Arduino.D2, Driver_motores.AIN2
  N2: Microcontrolador_Arduino.D3_PWM, Driver_motores.PWMA
  N3: Microcontrolador_Arduino.D4, Driver_motores.AIN1
  N4: Microcontrolador_Arduino.D6_PWM, R2.Pin_0
  N5: Microcontrolador_Arduino.D7, Driver_motores.STBY
  N6: Microcontrolador_Arduino.D8, Driver_motores.BIN1
  N7: Microcontrolador_Arduino.D9_PWM, R3.Pin_0
  N8: Microcontrolador_Arduino.D10_PWM/SS, R1.Pin_0
  N9: Microcontrolador_Arduino.D11_PWM/MOSI, Microcontrolador_Arduino.MOSI, Driver_motores.PWMB
  N10: Microcontrolador_Arduino.D12/MISO, Microcontrolador_Arduino.MISO, Driver_motores.BIN2
  5V: Microcontrolador_Arduino.USB_VIN, Driver_motores.VM
  N11: Driver_motores.B01, MB.pin_1
  N12: Driver_motores.B02, MB.pin_2
  N13: Driver_motores.A02, MA.pin_2
  N14: Driver_motores.A01, MA.pin_1
  N15: LED_RGB.red_anode, R1.Pin_1
  N16: LED_RGB.blue_anode, R2.Pin_1
  N17: LED_RGB.green_anode, R3.Pin_1

notes:
  Robot MODI, Conexiones de motores y LED RGB a Arduino FIO, 2.0
