# Fritzing sketch MODI_without_LED (saved by Fritzing 0.8.3b)

parts:
  Microcontrolador_Arduino = Arduino Fio (Funnel I/O)
  Driver_motores = TB6612FNG Breakout v11
  MB = DC Motor
  MA = DC Motor

nets:
  VCC: Microcontrolador_Arduino.VCC, Driver_motores.VCC
  N1: Microcontrolador_Arduino.D2, Driver_motores.AIN2
  N2: Microcontrolador_Arduino.D3_PWM, Driver_motores.PWMA
  N3: Microcontrolador_Arduino.D4, Driver_motores.AIN1
  N4: Microcontrolador_Arduino.D7, Driver_motores.STBY
  N5: Microcontrolador_Arduino.D8, Driver_motores.BIN1
  N6: Microcontrolador_Arduino.D11_PWM/MOSI, Microcontrolador_Arduino.MOSI, Driver_motores.PWMB
  N7: Microcontrolador_Arduino.D12/MISO, Microcontrolador_Arduino.MISO, Driver_motores.BIN2
  GND: Microcontrolador_Arduino.GND, Driver_motores.GND
  5V: Microcontrolador_Arduino.USB_VIN, Driver_motores.VM
  N8: Driver_motores.B01, MB.pin_1
  N9: Driver_motores.B02, MB.pin_2
  N10: Driver_motores.A02, MA.pin_2
  N11: Driver_motores.A01, MA.pin_1

notes:
  Robot MODI, Conexiones de motores y LED RGB a Arduino FIO, 2.0
